# Fritzing sketch 8-bit-counter-diagram (saved by Fritzing 0.8.7b)
breadboards: 1

parts:
  Part1 = Arduino Uno (Rev3)
  LED2 = LED - 5mm [color="Red (633nm)" package="5 mm [THT]"]
  LED3 = LED - 5mm [color="Red (633nm)" package="5 mm [THT]"]
  LED4 = LED - 5mm [color="Red (633nm)" package="5 mm [THT]"]
  R1 = Resistor [tolerance=±5% resistance=220 package=THT]
  R2 = Resistor [tolerance=±5% resistance=220 package=THT]
  R3 = Resistor [tolerance=±5% resistance=220 package=THT]
  LED5 = LED - 5mm [color="Red (633nm)" package="5 mm [THT]"]
  LED6 = LED - 5mm [color="Red (633nm)" package="5 mm [THT]"]
  LED7 = LED - 5mm [color="Red (633nm)" package="5 mm [THT]"]
  LED8 = LED - 5mm [color="Red (633nm)" package="5 mm [THT]"]
  R4 = Resistor [tolerance=±5% resistance=220 package=THT]
  R5 = Resistor [tolerance=±5% resistance=220 package=THT]
  R6 = Resistor [tolerance=±5% resistance=220 package=THT]
  R7 = Resistor [tolerance=±5% resistance=220 package=THT]
  LED9 = LED - 5mm [color="Red (633nm)" package="5 mm [THT]"]
  R8 = Resistor [tolerance=±5% resistance=220 package=THT]

nets:
  N1: Part1.D8, LED7.anode
  N2: Part1.D9_PWM, LED6.anode
  N3: Part1.D10_PWM/SS, LED5.anode
  N4: Part1.D11_PWM/MOSI, LED4.anode
  N5: Part1.D12/MISO, LED3.anode
  N6: Part1.D13/SCK, LED2.anode
  N7: Part1.D6_PWM, LED9.anode
  N8: Part1.D7, LED8.anode
  N9: LED2.cathode, R1.Pin_1
  N10: LED3.cathode, R2.Pin_1
  N11: LED4.cathode, R3.Pin_1
  N12: R1.Pin_0, R2.Pin_0, R3.Pin_0, R4.Pin_0, R5.Pin_0, R6.Pin_0, R7.Pin_0, R8.Pin_0
  N13: LED5.cathode, R4.Pin_1
  N14: LED6.cathode, R5.Pin_1
  N15: LED7.cathode, R6.Pin_1
  N16: LED8.cathode, R7.Pin_1
  N17: LED9.cathode, R8.Pin_1
